# Fritzing sketch esquematico (saved by Fritzing 0.9.3b)
breadboards: 1

parts:
  Part2 = Arduino Mega 2560 (Rev3)
  Part4 = LC Studio SD Card Module
  ZS-042_RTC2 = ZS-042 RTC Module
  R18 = Resistor [tolerance=±5% resistance=220 package="2010 [SMD]"]
  R19 = Resistor [tolerance=±5% resistance=330 package="2010 [SMD]"]
  R20 = Resistor [tolerance=±5% resistance=330 package="2010 [SMD]"]
  R21 = Resistor [tolerance=±5% resistance=330 package="2010 [SMD]"]
  R22 = Resistor [tolerance=±5% resistance=220 package="2010 [SMD]"]
  R23 = Resistor [tolerance=±5% resistance=220 package="2010 [SMD]"]

nets:
  N1: Part2.A4, ZS-042_RTC2.SDA
  N2: Part2.A5, ZS-042_RTC2.SCL
  GND: Part2.GND, Part4.GND, ZS-042_RTC2.GND, R19.Pin_1, R20.Pin_1, R21.Pin_1
  5V: Part2.5V, Part4.5V, ZS-042_RTC2.VCC
  N3: Part2.D50, Part4.MISO
  N4: Part2.D51, R23.Pin_0
  N5: Part2.D52, R22.Pin_0
  N6: Part2.D53, R18.Pin_0
  N7: Part4.CS, R18.Pin_1, R20.Pin_0
  N8: Part4.MOSI, R21.Pin_0, R23.Pin_1
  N9: Part4.SCK, R19.Pin_0, R22.Pin_1

custom parts:
  LC Studio SD Card Module: The LC Studio SD card module serves as an interface to an SD card. The module works at 3.3 volts and 5 volts. The SPI (Serial Peripheral Interface) protocol is used for communicating with the module.
